# Fritzing sketch diseño (saved by Fritzing 0.9.3b)
breadboards: 1

parts:
  Componente1 = Arduino Uno (Rev3)
  Componente2 = Bluetooth HC-05 Macho
  Componente3 = Thumb Joystick
  S1 = Momentary Switch [package=ksa_sealed_tac_switch]
  LED1 = smd LED [color="Orange (620nm)" package="0603 [SMD]"]
  R1 = Resistor [tolerance=±5% resistance=220 package="1206 [SMD]"]
  Componente4 = Thumb Joystick
  S2 = Momentary Switch [package=ksa_sealed_tac_switch]
  S3 = Momentary Switch [package=ksa_sealed_tac_switch]
  S4 = Momentary Switch [package=ksa_sealed_tac_switch]
  R2 = Resistor [tolerance=±5% resistance=220 package="1206 [SMD]"]
  R3 = Resistor [tolerance=±5% resistance=220 package="1206 [SMD]"]
  R4 = Resistor [tolerance=±5% resistance=220 package="1206 [SMD]"]
  R5 = Resistor [tolerance=±5% resistance=220 package="1206 [SMD]"]

nets:
  N1: Componente1.A0, Componente3.HORZ
  N2: Componente1.A1, Componente3.VERT
  N3: Componente1.A2, Componente4.HORZ
  N4: Componente1.A3, Componente4.VERT
  N5: Componente1.D8, S2.3, R3.Pin_1
  N6: Componente1.D9_PWM, S1.3, R2.Pin_1
  N7: Componente1.D10_PWM/SS, Componente2.TXD
  N8: Componente1.D11_PWM/MOSI, Componente2.RXD
  N9: Componente1.D6_PWM, S4.3, R5.Pin_1
  N10: Componente1.D7, S3.3, R4.Pin_1
  VCC: Componente1.5V, Componente2.VCC, Componente3.VCC, R1.Pin_1, Componente4.VCC, R2.Pin_0, R3.Pin_0, R4.Pin_0, R5.Pin_0
  GND: Componente1.GND, Componente2.GND, Componente3.GND, S1.1, LED1.anode, Componente4.GND, S2.1, S3.1, S4.1
  N11: LED1.cathode, R1.Pin_0
